# Fritzing sketch blinkLedfzz (saved by Fritzing 0.9.3b)
breadboards: 1

parts:
  Part1 = Arduino Uno (Rev3)
  R2 = Resistor [tolerance=±5% resistance=220 package=THT]
  R4 = Resistor [tolerance=±5% resistance=220 package=THT]
  R5 = Resistor [tolerance=±5% resistance=220 package=THT]
  R6 = Resistor [tolerance=±5% resistance=220 package=THT]
  R7 = Resistor [tolerance=±5% resistance=220 package=THT]
  LED1 = LED - 5mm [color="Red (633nm)" package="5 mm [THT]"]
  LED2 = LED - 5mm [color="Yellow (592nm)" package="5 mm [THT]"]
  LED3 = LED - 5mm [color="Green (565nm)" package="5 mm [THT]"]
  LED4 = LED - 5mm [color="Red (633nm)" package="5 mm [THT]"]
  LED5 = LED - 5mm [color="Green (570nm)" package="5 mm [THT]"]
  S3 = Pushbutton [package="[SMD]"]
  R8 = Resistor [tolerance=±5% resistance=220 package=THT]

nets:
  N1: Part1.D8, R7.Pin_1
  N2: Part1.D9_PWM, R8.Pin_0
  N3: Part1.D10_PWM/SS, R4.Pin_0
  N4: Part1.D11_PWM/MOSI, R5.Pin_0
  N5: Part1.GND, LED1.cathode, LED2.cathode, LED3.cathode, LED4.cathode, LED5.cathode
  N6: Part1.D7, R2.Pin_0
  N7: Part1.5V, S3.Pin_1, S3.Pin_2
  N8: R2.Pin_1, LED5.anode
  N9: R4.Pin_1, LED4.anode
  N10: R5.Pin_1, LED3.anode
  N11: R6.Pin_1, LED1.anode
  N12: R7.Pin_0, LED2.anode
  N13: S3.Pin_3, S3.Pin_4, R8.Pin_1

// code stored in the sketch: Untitled2.ino
// PROJECT 3 Interactive Traffic Light
int carRed = 12;
//configure traffic light
int carYellow = 11;
int carGreen = 10;

int button = 9;
//pin of button
int pedRed = 8;
//configure light for pedestrians
int pedGreen = 7;
int crossTime = 5000;
//time for pedestrians to pass unsigned
long changeTime;
//time that the button is pressed
void setup() {
//configure all LEDs as output
pinMode(carRed, OUTPUT);
pinMode(carYellow, OUTPUT);
pinMode(carGreen, OUTPUT);
pinMode(pedRed, OUTPUT);
pinMode(pedGreen, OUTPUT);
pinMode(button, INPUT);
//configure button as input
digitalWrite(carGreen, HIGH); //initialize green traffic light on

digitalWrite(pedRed, LOW); //initialize red pedestrian light off
}
void loop() {
int state = digitalRead(button);
// test if the button is pressed and if 5 seconds have passed after it is pressed lately.

if(state == HIGH && (millis() - changeTime)> 5000){
  changeLights();
  }
//carry out the function of changing LED

}

void changeLights() {
  digitalWrite(carGreen, LOW); //green traffic light off
  digitalWrite(carYellow, HIGH); //yellow traffic light on
  delay(2000);
  //wait for 2 secs
  digitalWrite(carYellow, LOW); // yellow traffic light off
  digitalWrite(carRed, HIGH);
  //red traffic light on
  delay(1000);
  // wait for 1 sec for safety reason
  digitalWrite(pedRed, LOW);
  //red pedestrian light off
  digitalWrite(pedGreen, HIGH); //light pedestrian light on
  delay(crossTime);
  // time for crossing street
  //blink green pedestrian light to notify pedestrians to pass soon
  for (int x=0; x<10; x++) {
  digitalWrite(pedGreen, HIGH);
  delay(250);
  digitalWrite(pedGreen, LOW);
  delay(250);
  }
  digitalWrite(pedRed, HIGH);
  //red pedestrian light on
  delay(500);
  digitalWrite(carRed, LOW);
  digitalWrite(carYellow, HIGH);
  delay(1000);
  delay(1000);
  digitalWrite(carYellow, LOW);
  digitalWrite(carGreen, HIGH);
  //red traffic light off
  //yellow traffic light on
  //yellow traffic light off
  //green traffic light on
  changeTime = millis();
  // record the duration since last change

  //back to the loop of main code
}
